// Logisim project 1530438.circ as structural Verilog: 5 circuits, main circuit main
module main (
  input  start,
  input  areset,
  output ready
);

  wire clk_out;
  wire [3:0] automate_1_ram_addr, automate_1_rom_addr;
  wire [15:0] automate_1_data, ram_1_data, rom_1_data;

  Clock clk (.out(clk_out));
  ROM #(.addrWidth(4), .dataWidth(16)) rom_1 (.addr(automate_1_rom_addr), .data(rom_1_data));  // open: sel
  RAM #(.addrWidth(4), .dataWidth(16), .bus("separate")) ram_1 (
    .addr(automate_1_ram_addr), .din(automate_1_data), .data(ram_1_data), .clk(clk_out), .clr(areset));  // open: str, sel, ld
  Automate automate_1 (
    .ram_addr(automate_1_ram_addr), .rom_Addr(automate_1_rom_addr), .data(automate_1_data), .Start(start),
    .CLK(clk_out), .RESET(areset), .READY(ready), .data_ram(ram_1_data), .data_ram_2(rom_1_data));
  LED led_1 (.in(ready));

  // Notes on the sheet:
  //   contents of rom_1 (hex, n*v repeats v):
  //   5 6 7 2 3 8 4 1 ffff 8000 7999 acdf
endmodule

module Automate (
  input  [15:0] data_ram,
  input  [15:0] data_ram_2,
  input  Start,
  input  RESET,
  input  CLK,
  output [3:0] ram_addr,
  output [3:0] rom_Addr,
  output [15:0] data,
  output READY
);

  wire comparator_1_eq, comparator_2_gt, comparator_3_eq, comparator_4_eq, comparator_5_eq,
       fsm_1_store_lo_to_ram, fsm_1_store_lo_to_ram_2, fsm_1_store_ro_to_buffer, or_1_out;
  wire [1:0] fsm_1_posram___1, fsm_1_posrom___1, fsm_1_store_buffer_to_lo;
  wire [3:0] adder_1_out, adder_2_out, multiplexer_2_out, multiplexer_3_out;
  wire [15:0] BUFFER_q, LO_q, multiplexer_4_out, multiplexer_5_out;

  Multiplexer #(.width(16)) multiplexer_1 (.in0(data_ram), .in1(LO_q), .out(data), .sel(or_1_out));  // open: en
  Adder #(.width(4)) adder_1 (.a(ram_addr), .b(4'b0001), .out(adder_1_out));  // open: cin, cout
  Multiplexer #(.select(2), .width(4)) multiplexer_2 (
    .in0(ram_addr), .in1(adder_1_out), .in2(4'b0000), .out(multiplexer_2_out), .sel(fsm_1_posram___1));  // open: in3, en
  Register #(.width(4), .trigger("falling")) posRAM (
    .D(multiplexer_2_out), .Q(ram_addr), .clk(CLK), .clr(RESET));  // open: en
  Comparator #(.width(16)) comparator_1 (.a(data_ram), .b({16{1'b0}}), .eq(comparator_1_eq));  // open: gt, lt
  Comparator #(.width(16)) comparator_2 (.a(LO_q), .b(data_ram), .gt(comparator_2_gt));  // open: eq, lt
  Adder #(.width(4)) adder_2 (.a(rom_Addr), .b(4'b0001), .out(adder_2_out));  // open: cin, cout
  FSM fsm_1 (
    .Start(Start), .posRom_0(comparator_3_eq), .LO__0(comparator_5_eq), .LO_RO(comparator_2_gt),
    .RO_0(comparator_1_eq), .posROM_16(comparator_4_eq), .posROM__0(fsm_1_posrom___1[1]),
    .posRAM__0(fsm_1_posram___1[1]), .posROM___1(fsm_1_posrom___1[0]),
    .Store_RO_to_Buffer(fsm_1_store_ro_to_buffer), .Store_Lo_to_RAM(fsm_1_store_lo_to_ram),
    .Store_Buffer_to_LO(fsm_1_store_buffer_to_lo[0]), .posRAM___1(fsm_1_posram___1[0]),
    .Store_LO_to_RAM_2(fsm_1_store_lo_to_ram_2), .Load_from_ROM(fsm_1_store_buffer_to_lo[1]), .READY(READY),
    .clk(CLK), .reset(RESET));
  or or_1 (or_1_out, fsm_1_store_lo_to_ram_2, fsm_1_store_lo_to_ram);
  Multiplexer #(.select(2), .width(4)) multiplexer_3 (
    .in0(rom_Addr), .in1(adder_2_out), .in2(4'b0000), .out(multiplexer_3_out), .sel(fsm_1_posrom___1));  // open: in3, en
  Register #(.width(4), .trigger("falling")) posROM (
    .D(multiplexer_3_out), .Q(rom_Addr), .clk(CLK), .clr(RESET));  // open: en
  Multiplexer #(.width(16)) multiplexer_4 (
    .in0(BUFFER_q), .in1(data_ram), .out(multiplexer_4_out), .sel(fsm_1_store_ro_to_buffer));  // open: en
  Comparator #(.width(4)) comparator_3 (.a(rom_Addr), .b(4'b0000), .eq(comparator_3_eq));  // open: gt, lt
  Comparator #(.width(4)) comparator_4 (.a(rom_Addr), .b(4'b1111), .eq(comparator_4_eq));  // open: gt, lt
  Register #(.width(16)) BUFFER (.D(multiplexer_4_out), .Q(BUFFER_q), .clk(CLK), .clr(RESET));  // open: en
  Multiplexer #(.select(2), .width(16)) multiplexer_5 (
    .in0(LO_q), .in1(BUFFER_q), .in2(data_ram_2), .out(multiplexer_5_out), .sel(fsm_1_store_buffer_to_lo));  // open: in3, en
  Register #(.width(16)) LO (.D(multiplexer_5_out), .Q(LO_q), .clk(CLK), .clr(RESET));  // open: en
  Comparator #(.width(16)) comparator_5 (.a(LO_q), .b({16{1'b0}}), .eq(comparator_5_eq));  // open: gt, lt

  // Notes on the sheet:
  //   RO=0
  //   LO>RO
  //   posROM=0
  //   posROM=16
  //   LO=0
endmodule

module FSM (
  input  Start,
  input  posRom_0,
  input  LO__0,
  input  LO_RO,
  input  RO_0,
  input  posROM_16,
  input  clk,
  input  reset,
  output posROM__0,
  output posRAM__0,
  output posROM___1,
  output Store_RO_to_Buffer,
  output Store_Lo_to_RAM,
  output Store_Buffer_to_LO,
  output posRAM___1,
  output Store_LO_to_RAM_2,
  output Load_from_ROM,
  output READY
);

  wire nsl_1_ns1, nsl_1_ns2, nsl_1_ns3, nsl_1_ns4;
  wire [3:0] ns1_q;

  NSL nsl_1 (
    .s4(ns1_q[3]), .s3(ns1_q[2]), .s2(ns1_q[1]), .s1(ns1_q[0]), .Start(Start), .posROMis0(posRom_0),
    .LOis0(LO__0), .LOgrRO(LO_RO), .ROis0(RO_0), .posROMis16(posROM_16), .ns4(nsl_1_ns4), .ns3(nsl_1_ns3),
    .ns2(nsl_1_ns2), .ns1(nsl_1_ns1));
  D_Flip_Flop ns4 (.clk(clk), .D(nsl_1_ns4), .Q(ns1_q[3]), .reset(reset));  // open: Qn, preset, en
  D_Flip_Flop ns3 (.clk(clk), .D(nsl_1_ns3), .Q(ns1_q[2]), .reset(reset));  // open: Qn, preset, en
  D_Flip_Flop ns2 (.clk(clk), .D(nsl_1_ns2), .Q(ns1_q[1]), .reset(reset));  // open: Qn, preset, en
  D_Flip_Flop ns1 (.clk(clk), .D(nsl_1_ns1), .Q(ns1_q[0]), .reset(reset));  // open: Qn, preset, en
  OutL outl_1 (
    .s4(ns1_q[3]), .s3(ns1_q[2]), .s2(ns1_q[1]), .s1(ns1_q[0]), .posROmset0(posROM__0),
    .posRAMset0(posRAM__0), .posROMp1(posROM___1), .ST_ROtBUF(Store_RO_to_Buffer),
    .St_LOtRAM(Store_Lo_to_RAM), .STBUFtLO(Store_Buffer_to_LO), .posRAMp1(posRAM___1),
    .ST_LOtRAM_2(Store_LO_to_RAM_2), .LDfROM(Load_from_ROM), .READY(READY));
endmodule

module NSL (
  input  s4,
  input  s3,
  input  s2,
  input  s1,
  input  Start,
  input  posROMis0,
  input  LOis0,
  input  LOgrRO,
  input  ROis0,
  input  posROMis16,
  output ns4,
  output ns3,
  output ns2,
  output ns1
);

  wire and_1_out, and_2_out, and_3_out, and_4_out, and_5_out, and_6_out, and_7_out, and_8_out, and_9_out,
       and_10_out, and_11_out, and_12_out, and_13_out, and_14_out, and_15_out, and_16_out, and_17_out,
       and_18_out, and_19_out, and_20_out, not_1_out, not_2_out, not_3_out, not_4_out, not_5_out, not_6_out,
       not_7_out, not_8_out, not_9_out, not_10_out, not_11_out, not_12_out, not_13_out, not_14_out,
       not_15_out, not_16_out, not_17_out, not_18_out, not_19_out, not_20_out, not_21_out, not_22_out,
       not_23_out, not_24_out, not_25_out, not_26_out, not_27_out, not_28_out, not_29_out;

  not not_1 (not_1_out, s4);
  not not_2 (not_2_out, s3);
  not not_3 (not_3_out, s2);
  not not_4 (not_4_out, s4);
  not not_5 (not_5_out, s3);
  not not_6 (not_6_out, s1);
  not not_7 (not_7_out, s3);
  not not_8 (not_8_out, s1);
  and and_1 (and_1_out, s2, s1);
  and and_2 (and_2_out, s3, s1);
  and and_3 (and_3_out, s3, s2);
  not not_9 (not_9_out, s4);
  not not_10 (not_10_out, s2);
  not not_11 (not_11_out, s2);
  not not_12 (not_12_out, s1);
  not not_13 (not_13_out, s1);
  not not_14 (not_14_out, LOis0);
  not not_15 (not_15_out, s3);
  not not_16 (not_16_out, s2);
  not not_17 (not_17_out, s1);
  not not_18 (not_18_out, s4);
  not not_19 (not_19_out, s1);
  not not_20 (not_20_out, s3);
  not not_21 (not_21_out, LOgrRO);
  not not_22 (not_22_out, s1);
  not not_23 (not_23_out, ROis0);
  not not_24 (not_24_out, s1);
  not not_25 (not_25_out, s2);
  not not_26 (not_26_out, s1);
  not not_27 (not_27_out, s1);
  not not_28 (not_28_out, posROMis0);
  not not_29 (not_29_out, s1);
  and and_4 (and_4_out, not_1_out, not_2_out, not_3_out, s1);
  and and_5 (and_5_out, not_4_out, not_5_out, s2, not_6_out);
  and and_6 (and_6_out, not_7_out, s2, not_8_out, LOis0);
  and and_7 (and_7_out, s4, s1, Start);
  or or_1 (ns3, and_1_out, and_2_out, and_3_out);
  and and_8 (and_8_out, not_9_out, not_10_out, s1);
  and and_9 (and_9_out, s3, not_11_out);
  and and_10 (and_10_out, s3, not_12_out);
  and and_11 (and_11_out, s4, s2, not_13_out, not_14_out);
  and and_12 (and_12_out, not_15_out, not_16_out, not_17_out, Start);
  and and_13 (and_13_out, not_18_out, s2, not_19_out, posROMis16);
  and and_14 (and_14_out, not_20_out, s2, s1, not_21_out);
  and and_15 (and_15_out, s3, not_22_out, not_23_out);
  and and_16 (and_16_out, s3, s2, not_24_out);
  and and_17 (and_17_out, s4, not_25_out, not_26_out);
  and and_18 (and_18_out, s4, not_27_out, not_28_out);
  and and_19 (and_19_out, s4, not_29_out, LOis0);
  and and_20 (and_20_out, s4, s1, Start);
  or or_2 (ns4, and_4_out, and_5_out, and_6_out, and_7_out);
  or or_3 (ns2, and_8_out, and_9_out, and_10_out, and_11_out);
  or or_4 (ns1, and_12_out, and_13_out, and_14_out, and_15_out, and_16_out, and_17_out, and_18_out, and_19_out, and_20_out);
endmodule

module OutL (
  input  s4,
  input  s3,
  input  s2,
  input  s1,
  output posROmset0,
  output posRAMset0,
  output posROMp1,
  output ST_ROtBUF,
  output St_LOtRAM,
  output STBUFtLO,
  output posRAMp1,
  output ST_LOtRAM_2,
  output LDfROM,
  output READY
);

  wire and_2_out, and_3_out, and_11_out, and_12_out, not_1_out, not_2_out, not_3_out, not_4_out, not_5_out,
       not_6_out, not_7_out, not_8_out, not_9_out, not_10_out, not_11_out, not_12_out, not_13_out,
       not_14_out, not_15_out, not_16_out, not_17_out, not_18_out, not_19_out, not_20_out, not_21_out,
       not_22_out, not_23_out, not_24_out;

  not not_1 (not_1_out, s4);
  not not_2 (not_2_out, s3);
  not not_3 (not_3_out, s2);
  not not_4 (not_4_out, s1);
  not not_5 (not_5_out, s3);
  and and_1 (posRAMset0, not_5_out, not_6_out, not_7_out);
  not not_6 (not_6_out, s2);
  not not_7 (not_7_out, s1);
  and and_2 (and_2_out, s4, not_8_out, not_9_out);
  not not_8 (not_8_out, s2);
  not not_9 (not_9_out, s1);
  and and_3 (and_3_out, s4, s3, not_10_out);
  not not_10 (not_10_out, s1);
  and and_4 (ST_ROtBUF, s3, not_11_out, s1);
  not not_11 (not_11_out, s2);
  and and_5 (St_LOtRAM, s3, s2, not_12_out);
  not not_12 (not_12_out, s1);
  and and_6 (STBUFtLO, s3, s2, s1);
  not not_13 (not_13_out, s2);
  and and_7 (posRAMp1, s3, not_13_out, not_14_out);
  not not_14 (not_14_out, s1);
  not not_15 (not_15_out, s4);
  not not_16 (not_16_out, s3);
  not not_17 (not_17_out, s1);
  not not_18 (not_18_out, s4);
  not not_19 (not_19_out, s3);
  not not_20 (not_20_out, s2);
  not not_21 (not_21_out, s4);
  not not_22 (not_22_out, s3);
  not not_23 (not_23_out, s2);
  not not_24 (not_24_out, s1);
  and and_8 (posROmset0, not_1_out, not_2_out, not_3_out, not_4_out);
  or or_1 (posROMp1, and_2_out, and_3_out);
  and and_9 (ST_LOtRAM_2, not_15_out, not_16_out, s2, not_17_out);
  and and_10 (LDfROM, not_18_out, not_19_out, not_20_out, s1);
  and and_11 (and_11_out, not_21_out, not_22_out, not_23_out, not_24_out);
  or or_2 (READY, and_11_out, and_12_out);
  and and_12 (and_12_out, s4, s1);
endmodule
